# Fritzing sketch fritzing_SICAKLIK_OLCUM_V6_SCHEMATİC (saved by Fritzing 0.9.3b)
breadboards: 1

parts:
  Parça1 = Arduino Uno (Rev3)
  DHT1 = DHT11 Humitidy and Temperature Sensor
  J1 = Piezo Speaker
  LED2 = LED - 3mm [color="Green (555nm)" package="3 mm [THT]"]
  LED3 = LED - 3mm [color="Red (633nm)" package="3 mm [THT]"]
  R1 = Resistor [tolerance=±5% resistance=220 package="0402 [SMD]"]
  R2 = Resistor [tolerance=±5% resistance=220 package="0402 [SMD]"]
  J2 = Basic Servo
  Parça2 = LCD1602-I2C

nets:
  N1: Parça1.D8, DHT1.DATA
  N2: Parça1.D9_PWM, J2.pulse
  N3: Parça1.D12/MISO, R2.Pin_1
  N4: Parça1.D13/SCK, R1.Pin_1
  N5: Parça1.A4/SDA, Parça2.SDA
  N6: Parça1.A5/SCL, Parça2.SCL
  VCC: Parça1.5V, DHT1.VDD, J2.vcc, Parça2.VCC
  GND: Parça1.GND, DHT1.GND, J1.pin1, LED2.cathode, LED3.cathode, J2.gnd, Parça2.GND
  N7: LED2.anode, R2.Pin_0
  N8: LED3.anode, R1.Pin_0

custom parts:
  DHT11 Humitidy and Temperature Sensor: DHT11 Humidity and Temperature Sensor
  LCD1602-I2C: A standard character display, usually with 2x16 characters. Comes in many colors with LCM1602 IIC attached.
